# Fritzing sketch drivebot (saved by Fritzing 0.9.3b)
breadboards: 1

parts:
  Part1 = Arduino Uno (Rev3)  # not connected
  S1 = Pushbutton [package="[THT]"]
  IC1 = MCP3008 8-channel 10-bit ADC [part_number=MCP3008]  # not connected
  IC2 = SHIFT REGISTER [package=dil16]  # not connected

nets:
  N1: S1.Pin_1, S1.Pin_2
  N2: S1.Pin_3, S1.Pin_4
